# Fritzing sketch wiring (saved by Fritzing 0.9.3b)
breadboards: 1

parts:
  Composant1 = Arduino Nano (Rev3.0)
  hc-sr1 = hc-sr04
  M1 = DC Motor
  M2 = DC Motor
  Composant2 = Arduino Motor Shield
  VCC2 = Battery block 9V
  VCC3 = Battery block 9V
  IC1 = Voltage Regulator [package=78xxl]
  J1 = Basic Servo

nets:
  N1: Composant1.D2, hc-sr1.Trig
  N2: Composant1.D3, hc-sr1.Echo
  N3: Composant1.D4, Composant2.D12
  N4: Composant1.D5, Composant2.D10
  N5: Composant1.D6, Composant2.D13
  N6: Composant1.D7, Composant2.D9
  N7: Composant1.D8, J1.pulse
  N8: Composant1.D9, Composant2.D11
  N9: Composant1.D10, Composant2.D3
  N10: Composant1.VIN, IC1.OUT
  GND: Composant1.GND, hc-sr1.GND, Composant2.GND, VCC2.-, VCC3.-, IC1.GND, J1.gnd
  5V: Composant1.5V, hc-sr1.VCC, Composant2.5V, J1.vcc
  N11: M1.pin_1, Composant2.OUT1
  N12: M1.pin_2, Composant2.OUT2
  N13: M2.pin_1, Composant2.OUT4
  N14: M2.pin_2, Composant2.OUT3
  N15: Composant2.VIN, VCC2.+
  N16: VCC3.+, IC1.IN

notes:
  This is not the exact component used, but it is close to it.
  Used one is L298.
